// Digital circuit breg.dig as structural Verilog
module breg (
  input  clk_breg,
  input  [3:0] a,
  input  [3:0] b,
  input  [3:0] c,
  input  [31:0] C_2,
  input  EscReg,
  output [31:0] A_2,
  output [31:0] B_2
);

  wire demultiplexer_1_out_1, demultiplexer_1_out_2, demultiplexer_1_out_3, demultiplexer_1_out_4,
       demultiplexer_1_out_5, demultiplexer_1_out_6, demultiplexer_1_out_7, demultiplexer_1_out_8,
       demultiplexer_1_out_9, demultiplexer_1_out_10, demultiplexer_1_out_11, demultiplexer_1_out_12,
       demultiplexer_1_out_13, demultiplexer_1_out_14, demultiplexer_1_out_15;
  wire [31:0] multiplexer_1_out, multiplexer_2_out, multiplexer_3_out, multiplexer_4_out, multiplexer_5_out,
       multiplexer_6_out, multiplexer_7_out, multiplexer_8_out, multiplexer_9_out, multiplexer_10_out,
       multiplexer_11_out, multiplexer_12_out, multiplexer_13_out, multiplexer_14_out, multiplexer_15_out,
       R1, R2, R3, R4, R5, R6, R7, R8, R9, R10, R11, R12, R13, R14, R15;

  Demultiplexer #(.Selector_Bits(4)) demultiplexer_1 (
    .sel(c), .in(EscReg), .out_1(demultiplexer_1_out_1), .out_2(demultiplexer_1_out_2),
    .out_3(demultiplexer_1_out_3), .out_4(demultiplexer_1_out_4), .out_5(demultiplexer_1_out_5),
    .out_6(demultiplexer_1_out_6), .out_7(demultiplexer_1_out_7), .out_8(demultiplexer_1_out_8),
    .out_9(demultiplexer_1_out_9), .out_10(demultiplexer_1_out_10), .out_11(demultiplexer_1_out_11),
    .out_12(demultiplexer_1_out_12), .out_13(demultiplexer_1_out_13), .out_14(demultiplexer_1_out_14),
    .out_15(demultiplexer_1_out_15));  // open: out_0
  Multiplexer #(.Bits(32)) multiplexer_1 (.sel(demultiplexer_1_out_1), .in_0(R1), .in_1(C_2), .out(multiplexer_1_out));
  Multiplexer #(.Bits(32)) multiplexer_2 (.sel(demultiplexer_1_out_2), .in_0(R2), .in_1(C_2), .out(multiplexer_2_out));
  Multiplexer #(.Bits(32)) multiplexer_3 (.sel(demultiplexer_1_out_3), .in_0(R3), .in_1(C_2), .out(multiplexer_3_out));
  Multiplexer #(.Bits(32)) multiplexer_4 (.sel(demultiplexer_1_out_4), .in_0(R4), .in_1(C_2), .out(multiplexer_4_out));
  Multiplexer #(.Bits(32)) multiplexer_5 (.sel(demultiplexer_1_out_5), .in_0(R5), .in_1(C_2), .out(multiplexer_5_out));
  Multiplexer #(.Bits(32)) multiplexer_6 (.sel(demultiplexer_1_out_6), .in_0(R6), .in_1(C_2), .out(multiplexer_6_out));
  Multiplexer #(.Bits(32)) multiplexer_7 (.sel(demultiplexer_1_out_7), .in_0(R7), .in_1(C_2), .out(multiplexer_7_out));
  Multiplexer #(.Bits(32)) multiplexer_8 (.sel(demultiplexer_1_out_8), .in_0(R8), .in_1(C_2), .out(multiplexer_8_out));
  Multiplexer #(.Bits(32)) multiplexer_9 (.sel(demultiplexer_1_out_9), .in_0(R9), .in_1(C_2), .out(multiplexer_9_out));
  Multiplexer #(.Bits(32)) multiplexer_10 (
    .sel(demultiplexer_1_out_10), .in_0(R10), .in_1(C_2), .out(multiplexer_10_out));
  Multiplexer #(.Bits(32)) multiplexer_11 (
    .sel(demultiplexer_1_out_11), .in_0(R11), .in_1(C_2), .out(multiplexer_11_out));
  Multiplexer #(.Bits(32)) multiplexer_12 (
    .sel(demultiplexer_1_out_12), .in_0(R12), .in_1(C_2), .out(multiplexer_12_out));
  Multiplexer #(.Bits(32)) multiplexer_13 (
    .sel(demultiplexer_1_out_13), .in_0(R13), .in_1(C_2), .out(multiplexer_13_out));
  Multiplexer #(.Bits(32)) multiplexer_14 (
    .sel(demultiplexer_1_out_14), .in_0(R14), .in_1(C_2), .out(multiplexer_14_out));
  Multiplexer #(.Bits(32)) multiplexer_15 (
    .sel(demultiplexer_1_out_15), .in_0(R15), .in_1(C_2), .out(multiplexer_15_out));
  D_FF #(.Bits(32)) d_ff_1 (.D(multiplexer_1_out), .C(clk_breg), .Q(R1));  // open: nQ
  D_FF #(.Bits(32)) d_ff_2 (.D(multiplexer_2_out), .C(clk_breg), .Q(R2));  // open: nQ
  D_FF #(.Bits(32)) d_ff_3 (.D(multiplexer_3_out), .C(clk_breg), .Q(R3));  // open: nQ
  D_FF #(.Bits(32)) d_ff_4 (.D(multiplexer_4_out), .C(clk_breg), .Q(R4));  // open: nQ
  D_FF #(.Bits(32)) d_ff_5 (.D(multiplexer_5_out), .C(clk_breg), .Q(R5));  // open: nQ
  D_FF #(.Bits(32)) d_ff_6 (.D(multiplexer_6_out), .C(clk_breg), .Q(R6));  // open: nQ
  D_FF #(.Bits(32)) d_ff_7 (.D(multiplexer_7_out), .C(clk_breg), .Q(R7));  // open: nQ
  D_FF #(.Bits(32)) d_ff_8 (.D(multiplexer_8_out), .C(clk_breg), .Q(R8));  // open: nQ
  D_FF #(.Bits(32)) d_ff_9 (.D(multiplexer_9_out), .C(clk_breg), .Q(R9));  // open: nQ
  D_FF #(.Bits(32)) d_ff_10 (.D(multiplexer_10_out), .C(clk_breg), .Q(R10));  // open: nQ
  D_FF #(.Bits(32)) d_ff_11 (.D(multiplexer_11_out), .C(clk_breg), .Q(R11));  // open: nQ
  D_FF #(.Bits(32)) d_ff_12 (.D(multiplexer_12_out), .C(clk_breg), .Q(R12));  // open: nQ
  D_FF #(.Bits(32)) d_ff_13 (.D(multiplexer_13_out), .C(clk_breg), .Q(R13));  // open: nQ
  D_FF #(.Bits(32)) d_ff_14 (.D(multiplexer_14_out), .C(clk_breg), .Q(R14));  // open: nQ
  D_FF #(.Bits(32)) d_ff_15 (.D(multiplexer_15_out), .C(clk_breg), .Q(R15));  // open: nQ
  Multiplexer #(.Selector_Bits(4), .Bits(32)) multiplexer_16 (
    .sel(a), .in_0({32{1'b0}}), .in_1(R1), .in_2(R2), .in_3(R3), .in_4(R4), .in_5(R5), .in_6(R6), .in_7(R7),
    .in_8(R8), .in_9(R9), .in_10(R10), .in_11(R11), .in_12(R12), .in_13(R13), .in_14(R14), .in_15(R15),
    .out(A_2));
  Multiplexer #(.Selector_Bits(4), .Bits(32)) multiplexer_17 (
    .sel(b), .in_0({32{1'b0}}), .in_1(R1), .in_2(R2), .in_3(R3), .in_4(R4), .in_5(R5), .in_6(R6), .in_7(R7),
    .in_8(R8), .in_9(R9), .in_10(R10), .in_11(R11), .in_12(R12), .in_13(R13), .in_14(R14), .in_15(R15),
    .out(B_2));

  // Other names for the same wires on the sheet: C_t[31:0] = C_2
endmodule
