// Digital circuit mico12.dig as structural Verilog
module mico12 (
  input  CLOCK
);

  wire B_ULA, EscRAM, EscReg, halt, zero_ULA;
  wire [1:0] C_BREG, ProxIP;
  wire [3:0] FUNC_ULA, MI_d_2;
  wire [15:0] breg_1_a_2, IP__plus__1_s, IP_q, multiplexer_1_out, multiplexer_2_out, multiplexer_3_out;
  wire [27:0] MI_d;
  wire [31:0] bitextender_1_out, breg_1_b_2, IP_plus_1_32_bits_out, M_d, multiplexer_4_out,
       multiplexer_5_out, ula_1_s;
  wire [31:16] breg_1_a_2_2;

  Multiplexer #(.Bits(16)) multiplexer_1 (
    .sel(zero_ULA), .in_0(IP__plus__1_s), .in_1(MI_d[15:0]), .out(multiplexer_1_out));
  Multiplexer #(.Selector_Bits(2), .Bits(16)) multiplexer_2 (
    .sel(ProxIP), .in_0(IP__plus__1_s), .in_1(MI_d[15:0]), .in_2(multiplexer_1_out), .in_3(breg_1_a_2),
    .out(multiplexer_2_out));
  Multiplexer #(.Bits(16)) multiplexer_3 (.sel(halt), .in_0({16{1'b0}}), .in_1(16'h1), .out(multiplexer_3_out));
  D_FF #(.Bits(16)) IP (.D(multiplexer_2_out), .C(CLOCK), .Q(IP_q));  // open: nQ
  Add #(.Bits(16)) IP__plus__1 (.a(multiplexer_3_out), .b(IP_q), .c_i(1'b0), .s(IP__plus__1_s));  // open: c_o
  // Probe IP on IP_q
  nand nand_1 (halt, MI_d_2[0], MI_d_2[1], MI_d_2[2], MI_d_2[3]);
  ROM #(.AddrBits(16), .Bits(32)) MI (.A(IP_q), .sel(1'b1), .D({MI_d_2, MI_d}));
  // Probe OPCODE on MI_d_2
  BitExtender #(.inputBits(17), .outputBits(32)) IP_plus_1_32_bits (
    .in({1'b0, IP__plus__1_s}), .out(IP_plus_1_32_bits_out));
  // Probe a on MI_d[27:24]
  ROM #(.AddrBits(4), .Bits(11)) Unidade_Controle (
    .A(MI_d_2), .sel(1'b1), .D({ProxIP, EscReg, B_ULA, FUNC_ULA, EscRAM, C_BREG}));
  // Probe b on MI_d[23:20]
  // Probe c on MI_d[19:16]
  breg breg_1 (
    .clk_breg(CLOCK), .a(MI_d[27:24]), .b(MI_d[23:20]), .c(MI_d[19:16]), .C_2(multiplexer_5_out),
    .EscReg(EscReg), .A_2({breg_1_a_2_2, breg_1_a_2}), .B_2(breg_1_b_2));
  BitExtender #(.inputBits(16), .outputBits(32)) bitextender_1 (.in(MI_d[15:0]), .out(bitextender_1_out));
  // Probe CONST on bitextender_1_out
  // Probe B on breg_1_b_2
  Multiplexer #(.Bits(32)) multiplexer_4 (
    .sel(B_ULA), .in_0(breg_1_b_2), .in_1(bitextender_1_out), .out(multiplexer_4_out));
  // Probe C on multiplexer_5_out
  // Probe A on {breg_1_a_2_2, breg_1_a_2}
  ula ula_1 (.A({breg_1_a_2_2, breg_1_a_2}), .B(multiplexer_4_out), .func(FUNC_ULA), .S(ula_1_s), .zero(zero_ULA));
  Multiplexer #(.Selector_Bits(2), .Bits(32)) multiplexer_5 (
    .sel(C_BREG), .in_0(ula_1_s), .in_1(M_d), .in_2(IP_plus_1_32_bits_out), .in_3({32{1'b0}}),
    .out(multiplexer_5_out));
  // Probe ULA on ula_1_s
  RAMDualPort #(.AddrBits(16), .Bits(32)) M (
    .A(ula_1_s[15:0]), .Din(breg_1_b_2), .str(EscRAM), .C(CLOCK), .ld(1'b1), .D(M_d));

  // Other names for the same wires on the sheet: clk = CLOCK

  // Notes on the sheet:
  //   contents of MI (hex, n*v repeats v):
  //   80040000,80050000,80060004,80070004,620000,8003000a,c00f001b,80080005
  //   ,64890000,e900002b,a7500028,80070004,520000,84030001,a30000,c00f0014
  //   ,150000,84040001,c0000009,80010000,800a0000,6a2b0000,eb00001a
  //   ,1310000,c0000016,df000000,800c0001,280000,a8c00000,a8c00001,800c0002
  //   ,6c390000,e900002a,8806ffff,8807fffe,96040000,97050000,45a0000
  //   ,a8a00000,88080001,c0000020,df000000,f0000000
  //   contents of Unidade_Controle (hex, n*v repeats v):
  //   100,108,0,110,118,120,128,130,180,181,84,0,302,600,408
endmodule
