// Digital circuit ula.dig as structural Verilog
module ula (
  input  [31:0] A,
  input  [31:0] B,
  input  [3:0] func,
  output [31:0] S,
  output zero
);

  wire [0:0] comparator_1_lt;
  wire [31:0] add_1_s, and_1_out, not_1_out, or_1_out, sub_1_s, xor_1_out;

  assign and_1_out = A & B;  // And and_1, 32 bits wide
  assign or_1_out = A | B;  // Or or_1, 32 bits wide
  assign xor_1_out = A ^ B;  // XOr xor_1, 32 bits wide
  Comparator #(.Bits(32), .Signed("true")) comparator_1 (.a(A), .b(B), .lt(comparator_1_lt[0]));  // open: gt, eq
  assign not_1_out = ~A;  // Not not_1, 32 bits wide
  Add #(.Bits(32)) add_1 (.a(A), .b(B), .c_i(1'b0), .s(add_1_s));  // open: c_o
  Sub #(.Bits(32)) sub_1 (.a(A), .b(B), .c_i(1'b0), .s(sub_1_s));  // open: c_o
  Multiplexer #(.Bits(32), .Selector_Bits(4)) multiplexer_1 (
    .sel(func), .in_0(add_1_s), .in_1(sub_1_s), .in_2(and_1_out), .in_3(or_1_out), .in_4(xor_1_out),
    .in_5({{31{1'b0}}, comparator_1_lt[0]}), .in_6(not_1_out), .in_7({32{1'b0}}), .in_8({32{1'b0}}),
    .in_9({32{1'b0}}), .in_10({32{1'b0}}), .in_11({32{1'b0}}), .in_12({32{1'b0}}), .in_13({32{1'b0}}),
    .in_14({32{1'b0}}), .in_15({32{1'b0}}), .out(S));
  Comparator #(.Bits(32)) comparator_2 (.a({32{1'b0}}), .b(S), .eq(zero));  // open: gt, lt
endmodule
